// Logisim project IR.circ as structural Verilog: 1 circuit, main circuit main
module main (
  input  [15:0] INP,
  input  LOAD,
  input  CLOCK,
  output [15:0] out_4
);

  Register #(.width(16)) register_1 (.D(INP), .en(LOAD), .Q(out_4), .clk(CLOCK));  // open: clr
endmodule
