// Logisim project Register_ref.circ as structural Verilog: 1 circuit, main circuit main
module main (
  input  D7I_prime_T3,
  input  [11:0] _12_Bits_data,
  output B0,
  output B1,
  output B2,
  output B3,
  output B4,
  output B5,
  output B6,
  output B7,
  output B8,
  output B9,
  output B10,
  output B11
);

  and and_1 (B0, D7I_prime_T3, _12_Bits_data[0]);
  and and_2 (B1, D7I_prime_T3, _12_Bits_data[1]);
  and and_3 (B2, D7I_prime_T3, _12_Bits_data[2]);
  and and_4 (B3, D7I_prime_T3, _12_Bits_data[3]);
  and and_5 (B4, D7I_prime_T3, _12_Bits_data[4]);
  and and_6 (B5, D7I_prime_T3, _12_Bits_data[5]);
  and and_7 (B6, D7I_prime_T3, _12_Bits_data[6]);
  and and_8 (B7, D7I_prime_T3, _12_Bits_data[7]);
  and and_9 (B8, D7I_prime_T3, _12_Bits_data[8]);
  and and_10 (B9, D7I_prime_T3, _12_Bits_data[9]);
  and and_11 (B10, D7I_prime_T3, _12_Bits_data[10]);
  and and_12 (B11, D7I_prime_T3, _12_Bits_data[11]);
endmodule
