// Logisim project incrReg_12Bit.circ as structural Verilog: 1 circuit, main circuit main
module main (
  input  [11:0] INP,
  input  LOAD,
  input  INC,
  input  CLR,
  input  CLOCK,
  output [11:0] out_6
);

  wire multiplexer_2_out, undriven;
  wire [11:0] adder_1_out, multiplexer_1_out;

  Adder #(.width(12)) adder_1 (.a(12'h1), .b(out_6), .out(adder_1_out), .cin(undriven));  // open: cout
  Multiplexer #(.width(12)) multiplexer_1 (
    .in0(INP), .in1(adder_1_out), .out(multiplexer_1_out), .sel(INC));  // open: en
  Multiplexer multiplexer_2 (.in0(LOAD), .in1(INC), .out(multiplexer_2_out), .sel(INC));  // open: en
  Register #(.width(12)) register_1 (.D(multiplexer_1_out), .en(multiplexer_2_out), .Q(out_6), .clk(CLOCK), .clr(CLR));
endmodule
