// Logisim project incrReg_16Bit.circ as structural Verilog: 1 circuit, main circuit main
module main (
  input  [15:0] INP,
  input  LOAD,
  input  INC,
  input  CLR,
  input  CLOCK,
  output [15:0] out_6
);

  wire multiplexer_2_out;
  wire [15:0] adder_1_out, multiplexer_1_out;

  Adder #(.width(16)) adder_1 (.a(16'h1), .b(out_6), .out(adder_1_out));  // open: cin, cout
  Multiplexer #(.width(16)) multiplexer_1 (
    .in0(INP), .in1(adder_1_out), .out(multiplexer_1_out), .sel(INC));  // open: en
  Multiplexer multiplexer_2 (.in0(LOAD), .in1(INC), .out(multiplexer_2_out), .sel(INC));  // open: en
  Register #(.width(16)) register_1 (.D(multiplexer_1_out), .en(multiplexer_2_out), .Q(out_6), .clk(CLOCK), .clr(CLR));
endmodule
