// Logisim project main.circ as structural Verilog: 1 circuit, main circuit main
module main (
  input  FGO,
  input  FGI,
  input  in_3,
  input  clear,
  input  [7:0] INPR,
  input  Inc,
  input  clear_2,
  output R,
  output I,
  output [2:0] OPCODE,
  output IEN,
  output [11:0] OPERAND,
  output [2:0] out_13,
  output E
);

  wire and_1_out, CLOCK_out, D7I_prime_T3_out, D7IT3_out, decoder_1_out0, decoder_1_out1, decoder_1_out2,
       decoder_1_out3, decoder_1_out4, decoder_1_out5, decoder_1_out6, decoder_1_out7, FGI_q, FGO_q,
       main_1_t0, main_1_t1, main_1_t2, main_1_t3, main_1_t4, main_1_t5, main_1_t6, main_1_t7, main_2_ien__0,
       main_2_ien__1, main_2_ld_dr, main_2_ld_ir, main_2_ld_tr, main_2_rj, main_2_rk, main_2_s__0,
       main_2_sc__0, not_1_out, not_2_out, not_3_out, S_q, SC_q, VAL_EXTR_ac_15, VAL_EXTR_ac_value,
       VAL_EXTR_e_2, VAL_EXTR_fgi_2, VAL_EXTR_fgo_2;
  wire [1:0] main_2_e__e_prime, main_2_inc_ac, main_2_read;
  wire [2:0] main_2_inc_ar, main_2_inc_pc;
  wire [3:0] ALU_ac, ALU_ac_2, ALU_ac_3, ALU_ac_4, AR_out_6, AR_out_6_2, AR_out_6_3, DR_out_6, DR_out_6_2,
       DR_out_6_3, DR_out_6_4, multiplexer_1_out, multiplexer_1_out_2, multiplexer_1_out_3,
       multiplexer_1_out_4, undriven;
  wire [5:0] I_O_REF_b6;
  wire [7:0] main_2_and;
  wire [11:0] REGIST_REF_b0;
  wire [15:0] PC_out_6, RAM_out, TR_out_6;
  wire [19:0] MEMORY_REFERENCE_r_prime_t0;

  Decoder #(.select(3)) decoder_1 (
    .out0(decoder_1_out0), .out1(decoder_1_out1), .out2(decoder_1_out2), .out3(decoder_1_out3),
    .out4(decoder_1_out4), .out5(decoder_1_out5), .out6(decoder_1_out6), .out7(decoder_1_out7), .sel(OPCODE));  // open: en
  not not_1 (not_1_out, I);
  and D7I_prime_T3 (D7I_prime_T3_out, decoder_1_out7, not_1_out, main_1_t3);
  and D7IT3 (D7IT3_out, decoder_1_out7, I, main_1_t3);
  COUNTER_main main_1 (
    .CLOCK(and_1_out), .CLEAR(SC_q), .T0(main_1_t0), .T1(main_1_t1), .T2(main_1_t2), .T3(main_1_t3),
    .T4(main_1_t4), .T5(main_1_t5), .T6(main_1_t6), .T7(main_1_t7));
  Register_ref_main REGIST_REF (
    .B0(REGIST_REF_b0[0]), .B1(REGIST_REF_b0[1]), .B2(REGIST_REF_b0[2]), .B3(REGIST_REF_b0[3]),
    .B4(REGIST_REF_b0[4]), .B5(REGIST_REF_b0[5]), .B6(REGIST_REF_b0[6]), .B7(REGIST_REF_b0[7]),
    .B8(REGIST_REF_b0[8]), .B9(REGIST_REF_b0[9]), .B10(REGIST_REF_b0[10]), .B11(REGIST_REF_b0[11]),
    .D7I_prime_T3(D7I_prime_T3_out), ._12_Bits_data(OPERAND));
  ALU_main ALU (
    .DR({DR_out_6_4, DR_out_6_3, DR_out_6_2, DR_out_6}), .INPR(INPR), .INP_8(main_2_and), .E(E),
    .AC({ALU_ac_4, ALU_ac_3, ALU_ac_2, ALU_ac}), .Eval(main_2_e__e_prime), .Inc(main_2_inc_ac[0]),
    .CLEAN(main_2_inc_ac[1]), .CLK(and_1_out));
  incrReg_12Bit_main AR (
    .INP({multiplexer_1_out_3, multiplexer_1_out_2, multiplexer_1_out}),
    .out_6({AR_out_6_3, AR_out_6_2, AR_out_6}), .INC(main_2_inc_ar[0]), .LOAD(main_2_inc_ar[1]),
    .CLR(main_2_inc_ar[2]), .CLOCK(and_1_out));
  incrReg_12Bit_main PC (
    .INP({multiplexer_1_out_3, multiplexer_1_out_2, multiplexer_1_out}), .out_6(PC_out_6[11:0]),
    .INC(main_2_inc_pc[0]), .LOAD(main_2_inc_pc[1]), .CLR(main_2_inc_pc[2]), .CLOCK(and_1_out));
  incrReg_16Bit_main DR (
    .INP({multiplexer_1_out_4, multiplexer_1_out_3, multiplexer_1_out_2, multiplexer_1_out}),
    .out_6({DR_out_6_4, DR_out_6_3, DR_out_6_2, DR_out_6}), .INC(in_3), .LOAD(main_2_ld_dr), .CLR(clear),
    .CLOCK(and_1_out));
  IR_main IR (
    .INP({multiplexer_1_out_4, multiplexer_1_out_3, multiplexer_1_out_2, multiplexer_1_out}),
    .out_4({I, OPCODE, OPERAND}), .LOAD(main_2_ld_ir), .CLOCK(and_1_out));
  incrReg_16Bit_main TR (
    .INP({multiplexer_1_out_4, multiplexer_1_out_3, multiplexer_1_out_2, multiplexer_1_out}),
    .out_6(TR_out_6), .INC(Inc), .LOAD(main_2_ld_tr), .CLR(clear_2), .CLOCK(and_1_out));
  memoryRAM_main RAM (
    .AC({AR_out_6_3, AR_out_6_2, AR_out_6}),
    .DATA({multiplexer_1_out_4, multiplexer_1_out_3, multiplexer_1_out_2, multiplexer_1_out}), .OUT(RAM_out),
    .WRITE(main_2_read[1]), .CLOCK(and_1_out), .READ(main_2_read[0]));
  IO_Reference_main I_O_REF (
    .B6(I_O_REF_b6[0]), .B7(I_O_REF_b6[1]), .B8(I_O_REF_b6[2]), .B9(I_O_REF_b6[3]), .B10(I_O_REF_b6[4]),
    .B11(I_O_REF_b6[5]), .D7IT3(D7IT3_out), ._12bit_data(OPERAND));
  and and_1 (and_1_out, CLOCK_out, not_2_out);
  not not_2 (not_2_out, S_q);
  Clock CLOCK (.out(CLOCK_out));
  Hex_Digit_Display hex_digit_display_1 (.value(undriven));  // open: dp
  Hex_Digit_Display hex_digit_display_2 (.value(PC_out_6[15:12]));  // open: dp
  Hex_Digit_Display hex_digit_display_3 (.value(DR_out_6_4));  // open: dp
  Hex_Digit_Display hex_digit_display_4 (.value(ALU_ac_4));  // open: dp
  Hex_Digit_Display hex_digit_display_5 (.value({I, OPCODE}));  // open: dp
  Hex_Digit_Display hex_digit_display_6 (.value(TR_out_6[15:12]));  // open: dp
  Hex_Digit_Display hex_digit_display_7 (.value(multiplexer_1_out_4));  // open: dp
  Hex_Digit_Display hex_digit_display_8 (.value(AR_out_6_3));  // open: dp
  Hex_Digit_Display hex_digit_display_9 (.value(PC_out_6[11:8]));  // open: dp
  Hex_Digit_Display hex_digit_display_10 (.value(DR_out_6_3));  // open: dp
  Hex_Digit_Display hex_digit_display_11 (.value(ALU_ac_3));  // open: dp
  Hex_Digit_Display hex_digit_display_12 (.value(OPERAND[11:8]));  // open: dp
  Hex_Digit_Display hex_digit_display_13 (.value(TR_out_6[11:8]));  // open: dp
  Hex_Digit_Display hex_digit_display_14 (.value(multiplexer_1_out_3));  // open: dp
  Hex_Digit_Display hex_digit_display_15 (.value(AR_out_6));  // open: dp
  Hex_Digit_Display hex_digit_display_16 (.value(AR_out_6_2));  // open: dp
  Hex_Digit_Display hex_digit_display_17 (.value(PC_out_6[7:4]));  // open: dp
  Hex_Digit_Display hex_digit_display_18 (.value(PC_out_6[3:0]));  // open: dp
  Hex_Digit_Display hex_digit_display_19 (.value(DR_out_6_2));  // open: dp
  Hex_Digit_Display hex_digit_display_20 (.value(DR_out_6));  // open: dp
  Hex_Digit_Display hex_digit_display_21 (.value(ALU_ac_2));  // open: dp
  Hex_Digit_Display hex_digit_display_22 (.value(ALU_ac));  // open: dp
  Hex_Digit_Display hex_digit_display_23 (.value(OPERAND[7:4]));  // open: dp
  Hex_Digit_Display hex_digit_display_24 (.value(OPERAND[3:0]));  // open: dp
  Hex_Digit_Display hex_digit_display_25 (.value(TR_out_6[7:4]));  // open: dp
  Hex_Digit_Display hex_digit_display_26 (.value(TR_out_6[3:0]));  // open: dp
  Hex_Digit_Display hex_digit_display_27 (.value(multiplexer_1_out));  // open: dp
  Hex_Digit_Display hex_digit_display_28 (.value(multiplexer_1_out_2));  // open: dp
  D_Flip_Flop u_FGO (.clk(and_1_out), .D(FGO), .Q(FGO_q));  // open: Qn, preset, en, reset
  D_Flip_Flop u_FGI (.clk(and_1_out), .D(FGI), .Q(FGI_q));  // open: Qn, preset, en, reset
  memory_ref_main MEMORY_REFERENCE (
    .R_prime_T0(MEMORY_REFERENCE_r_prime_t0[0]), .R_prime_T1(MEMORY_REFERENCE_r_prime_t0[1]),
    .R_prime_T2(MEMORY_REFERENCE_r_prime_t0[2]), .D7_prime_IT3(MEMORY_REFERENCE_r_prime_t0[3]),
    .T0_prime_T1_prime_T2_prime_IEN__FGO_FGI(MEMORY_REFERENCE_r_prime_t0[4]),
    .RT0(MEMORY_REFERENCE_r_prime_t0[5]), .RT1(MEMORY_REFERENCE_r_prime_t0[6]),
    .RT2(MEMORY_REFERENCE_r_prime_t0[7]), .D0T4(MEMORY_REFERENCE_r_prime_t0[8]),
    .D0T5(MEMORY_REFERENCE_r_prime_t0[9]), .D1T4(MEMORY_REFERENCE_r_prime_t0[10]),
    .D1T5(MEMORY_REFERENCE_r_prime_t0[11]), .D2T4(MEMORY_REFERENCE_r_prime_t0[12]),
    .D2T5(MEMORY_REFERENCE_r_prime_t0[13]), .D3T4(MEMORY_REFERENCE_r_prime_t0[14]),
    .D4T4(MEMORY_REFERENCE_r_prime_t0[15]), .D5T4(MEMORY_REFERENCE_r_prime_t0[16]),
    .D5T5(MEMORY_REFERENCE_r_prime_t0[17]), .D6T4(MEMORY_REFERENCE_r_prime_t0[18]),
    .D6T5(MEMORY_REFERENCE_r_prime_t0[19]), .T0(main_1_t0), .T1(main_1_t1), .T2(main_1_t2), .T3(main_1_t3),
    .T4(main_1_t4), .T5(main_1_t5), .T6(main_1_t6), .T7(main_1_t7), .D0(decoder_1_out0), .D1(decoder_1_out1),
    .D2(decoder_1_out2), .D3(decoder_1_out3), .D4(decoder_1_out4), .D5(decoder_1_out5), .D6(decoder_1_out6),
    .D7(decoder_1_out7), .R(R), .IEN(IEN), .FGI(FGI), .FGO(FGO), .S(S_q), .E(E), .I(I));
  Multiplexer #(.select(3), .width(16)) multiplexer_1 (
    .in1({undriven, AR_out_6_3, AR_out_6_2, AR_out_6}), .in2(PC_out_6),
    .in3({DR_out_6_4, DR_out_6_3, DR_out_6_2, DR_out_6}), .in4({ALU_ac_4, ALU_ac_3, ALU_ac_2, ALU_ac}),
    .in5({I, OPCODE, OPERAND}), .in6(TR_out_6), .in7(RAM_out),
    .out({multiplexer_1_out_4, multiplexer_1_out_3, multiplexer_1_out_2, multiplexer_1_out}), .sel(out_13));  // open: in0, en
  val_Extracter_main VAL_EXTR (
    .AC({ALU_ac_4, ALU_ac_3, ALU_ac_2, ALU_ac}), .E(E), .FGO(FGO_q), .FGI(FGI_q),
    .AC_VALUE(VAL_EXTR_ac_value), .AC_15(VAL_EXTR_ac_15), .E_2(VAL_EXTR_e_2), .FGO_2(VAL_EXTR_fgo_2),
    .FGI_2(VAL_EXTR_fgi_2));
  CU_main main_2 (
    .AC_Val(VAL_EXTR_ac_value), .AC15(VAL_EXTR_ac_15), .E(VAL_EXTR_e_2), .FGO(VAL_EXTR_fgo_2),
    .FGI(VAL_EXTR_fgi_2), .R_prime_T0(MEMORY_REFERENCE_r_prime_t0[0]),
    .R_prime_T1(MEMORY_REFERENCE_r_prime_t0[1]), .R_prime_T2(MEMORY_REFERENCE_r_prime_t0[2]),
    .D7_prime_IT3(MEMORY_REFERENCE_r_prime_t0[3]),
    .T1_prime_T2_prime_T3_prime(MEMORY_REFERENCE_r_prime_t0[4]), .RT0(MEMORY_REFERENCE_r_prime_t0[5]),
    .RT1(MEMORY_REFERENCE_r_prime_t0[6]), .RT2(MEMORY_REFERENCE_r_prime_t0[7]),
    .D0T4(MEMORY_REFERENCE_r_prime_t0[8]), .D0T5(MEMORY_REFERENCE_r_prime_t0[9]),
    .D1T4(MEMORY_REFERENCE_r_prime_t0[10]), .D1T5(MEMORY_REFERENCE_r_prime_t0[11]),
    .D2T4(MEMORY_REFERENCE_r_prime_t0[12]), .D2T5(MEMORY_REFERENCE_r_prime_t0[13]),
    .D3T4(MEMORY_REFERENCE_r_prime_t0[14]), .D4T4(MEMORY_REFERENCE_r_prime_t0[15]),
    .D5T4(MEMORY_REFERENCE_r_prime_t0[16]), .D5T5(MEMORY_REFERENCE_r_prime_t0[17]),
    .D6T4(MEMORY_REFERENCE_r_prime_t0[18]), .D6T5(MEMORY_REFERENCE_r_prime_t0[19]), .rB0(REGIST_REF_b0[0]),
    .rB1(REGIST_REF_b0[1]), .rB2(REGIST_REF_b0[2]), .rB3(REGIST_REF_b0[3]), .rB4(REGIST_REF_b0[4]),
    .rB5(REGIST_REF_b0[5]), .rB6(REGIST_REF_b0[6]), .rB7(REGIST_REF_b0[7]), .rB8(REGIST_REF_b0[8]),
    .rB9(REGIST_REF_b0[9]), .rB10(REGIST_REF_b0[10]), .rB11(REGIST_REF_b0[11]), .pB6(I_O_REF_b6[0]),
    .pB7(I_O_REF_b6[1]), .pB8(I_O_REF_b6[2]), .pB9(I_O_REF_b6[3]), .pB10(I_O_REF_b6[4]),
    .pB11(I_O_REF_b6[5]), .INC_AR(main_2_inc_ar[0]), .LD_AR(main_2_inc_ar[1]), .CLR_AR(main_2_inc_ar[2]),
    .RJ(main_2_rj), .Rk(main_2_rk), .INC_PC(main_2_inc_pc[0]), .LD_PC(main_2_inc_pc[1]),
    .CLR_PC(main_2_inc_pc[2]), .READ(main_2_read[0]), .WRITE(main_2_read[1]), .LD_DR(main_2_ld_dr),
    .LD_IR(main_2_ld_ir), .LD_TR(main_2_ld_tr), .INC_AC(main_2_inc_ac[0]), .CLR_AC(main_2_inc_ac[1]),
    .S0(out_13[0]), .S1(out_13[1]), .S2(out_13[2]), .S__0(main_2_s__0), .AND(main_2_and[0]),
    .ADD(main_2_and[1]), .SUB(main_2_and[2]), .DR(main_2_and[3]), .INPR(main_2_and[4]), .SHR(main_2_and[6]),
    .IEN__0(main_2_ien__0), .COM(main_2_and[5]), .IEN__1(main_2_ien__1), .SHL(main_2_and[7]),
    .E__E_prime(main_2_e__e_prime[0]), .E__0(main_2_e__e_prime[1]), .SC__0(main_2_sc__0));
  D_Flip_Flop S (.clk(and_1_out), .D(main_2_s__0), .Q(S_q));  // open: Qn, preset, en, reset
  J_K_Flip_Flop SC (.J(main_2_sc__0), .clk(and_1_out), .K(not_3_out), .Q(SC_q));  // open: Qn, preset, en, reset
  not not_3 (not_3_out, main_2_sc__0);
  J_K_Flip_Flop R_FLAG (.J(main_2_rj), .clk(and_1_out), .K(main_2_rk), .Q(R));  // open: Qn, preset, en, reset
  J_K_Flip_Flop IEN_FLAG (
    .J(main_2_ien__0), .clk(and_1_out), .K(main_2_ien__1), .Q(IEN));  // open: Qn, preset, en, reset

  // Notes on the sheet:
  //   AR
  //   PC
  //   DR
  //   AC
  //   IR
  //   TR
  //   OUTR
endmodule
