// Logisim project memoryRAM.circ as structural Verilog: 1 circuit, main circuit main
module main (
  input  [11:0] AC,
  input  [15:0] DATA,
  input  CLOCK,
  input  WRITE,
  input  READ,
  output [15:0] OUT
);

  RAM #(.addrWidth(12), .dataWidth(16), .bus("separate")) ram_1 (
    .addr(AC), .din(DATA), .data(OUT), .str(WRITE), .clk(CLOCK), .ld(READ));  // open: sel, clr
endmodule
