// Logisim project val-Extracter.circ as structural Verilog: 1 circuit, main circuit main
module main (
  input  [15:0] AC,
  input  E,
  input  FGO,
  input  FGI,
  output AC_VALUE,
  output AC_15,
  output E_2,
  output FGO_2,
  output FGI_2
);

  or or_1 (AC_VALUE, AC[0], AC[1], AC[2], AC[3], AC[4], AC[5], AC[6], AC[7], AC[8], AC[9], AC[10], AC[11], AC[12], AC[13], AC[14], AC[15]);

  assign AC_15 = AC[15];
  assign E_2 = E;
  assign FGI_2 = FGI;
  assign FGO_2 = FGO;
endmodule
